// Logisim project LIN_elements.circ as structural Verilog: 1 circuit, main circuit main
module main (
  output BREAK_Slave,
  output out_2,
  output out_3,
  output out_4,
  output out_5,
  output out_6,
  output out_7,
  output out_8,
  output out_9,
  output out_10,
  output out_11,
  output out_12,
  output out_13,
  output out_14,
  output Master,
  output SYNC_Slave,
  output out_17,
  output out_18,
  output out_19,
  output out_20,
  output out_21,
  output out_22,
  output out_23,
  output out_24,
  output out_25,
  output out_26,
  output out_27,
  output out_28,
  output PID_Slave,
  output out_30,
  output out_31,
  output out_32,
  output out_33,
  output out_34,
  output out_35,
  output out_36,
  output out_37,
  output out_38,
  output out_39,
  output Slave
);

  wire and_1_out, and_2_out, and_3_out, and_4_out, and_5_out, and_6_out, and_7_out, and_8_out, and_9_out,
       and_10_out, and_11_out, and_12_out, and_13_out, and_14_out, and_15_out, and_16_out, and_17_out,
       and_18_out, and_19_out, and_20_out, and_21_out, and_22_out, and_23_out, and_24_out, and_25_out,
       and_26_out, and_27_out, and_28_out, and_29_out, and_30_out, and_31_out, and_32_out, and_33_out,
       and_34_out, and_35_out, and_36_out, and_37_out, and_38_out, and_39_out, and_40_out, and_41_out,
       and_42_out, and_43_out, and_44_out, and_45_out, and_46_out, and_47_out, and_48_out, and_49_out,
       and_50_out, and_51_out, and_52_out, and_53_out, and_54_out, and_55_out, and_56_out, and_57_out,
       and_58_out, and_59_out, clock_1_out, clock_2_out, comparator_1_eq, comparator_2_eq, comparator_3_eq,
       comparator_4_eq, comparator_5_eq, comparator_6_eq, comparator_7_eq, comparator_8_eq, comparator_9_eq,
       comparator_10_eq, comparator_11_eq, comparator_11_gt, D1_q, D2_q, D2_qn, D3_q, d_ff_1_q, d_ff_2_q,
       d_ff_3_q, d_ff_4_q, d_ff_5_q, d_ff_6_q, d_ff_7_q, d_ff_8_q, d_ff_9_q, d_ff_10_q, d_ff_11_q, d_ff_12_q,
       d_ff_13_q, d_ff_36_q, d_ff_38_q, d_ff_40_q, d_ff_53_q, d_ff_54_q, d_ff_55_q, d_ff_56_q, d_ff_57_q,
       d_ff_58_q, d_ff_59_q, d_ff_60_q, multiplexer_1_out, not_1_out, not_2_out, not_3_out, not_4_out,
       not_5_out, not_6_out, not_7_out, not_8_out, not_9_out, not_10_out, not_11_out, not_12_out, not_13_out,
       not_14_out, not_15_out, not_16_out, not_17_out, not_18_out, not_19_out, not_20_out, not_21_out,
       not_22_out, OR1_out, or_1_out, or_2_out, or_3_out, or_4_out, or_5_out, or_8_out, or_9_out, or_10_out,
       or_11_out, or_12_out, or_13_out, or_14_out, or_15_out, or_16_out, or_17_out, or_18_out, or_19_out,
       or_20_out, or_21_out, xor_1_out, xor_2_out;
  wire [1:0] or_6_out;
  wire [2:0] j_k_ff_21_q;
  wire [3:0] j_k_ff_1_q, j_k_ff_5_q, j_k_ff_7_q, j_k_ff_8_q, j_k_ff_17_q, JK1_q, JK5_q;

  Clock #(.phaseOffset(1)) clock_1 (.out(clock_1_out));
  not not_1 (not_1_out, clock_1_out);
  J_K_Flip_Flop JK1 (.J(1'b1), .K(1'b1), .clk(clock_1_out), .Q(JK1_q[0]), .reset(d_ff_8_q));  // open: Qn, preset
  D_Flip_Flop D2 (.D(D2_qn), .clk(clock_1_out), .Q(D2_q), .Qn(D2_qn));  // open: preset, reset
  J_K_Flip_Flop JK5 (.J(OR1_out), .K(OR1_out), .clk(clock_1_out), .Q(JK5_q[0]), .reset(d_ff_8_q));  // open: Qn, preset
  not not_2 (not_2_out, xor_1_out);
  ExactlyOne xor_1 (.out(xor_1_out), .in0(1'b1), .in1(1'b0), .in2(1'b0), .in3(1'b0));
  and and_1 (and_1_out, clock_1_out, not_1_out);
  J_K_Flip_Flop JK2 (
    .J(JK1_q[0]), .K(JK1_q[0]), .clk(clock_1_out), .Q(JK1_q[1]), .reset(d_ff_8_q));  // open: Qn, preset
  and and_2 (and_2_out, OR1_out, D2_q);
  J_K_Flip_Flop JK6 (
    .J(JK5_q[0]), .K(JK5_q[0]), .clk(clock_1_out), .Q(JK5_q[1]), .reset(d_ff_8_q));  // open: Qn, preset
  and and_3 (and_3_out, 1'b1, not_3_out);
  not not_3 (not_3_out, comparator_2_eq);
  and and_4 (and_4_out, comparator_2_eq, 1'b1);
  ExactlyOne xor_2 (.out(xor_2_out), .in0(1'b0), .in1(1'b0), .in2(1'b0), .in3(1'b0));
  or OR1 (OR1_out, and_1_out, D1_q);
  and and_5 (and_5_out, JK1_q[1], JK1_q[0]);
  not not_4 (not_4_out, and_2_out);
  and and_6 (and_6_out, JK5_q[1], JK5_q[0]);
  D_Flip_Flop d_ff_1 (.D(or_1_out), .clk(clock_1_out), .Q(d_ff_1_q));  // open: Qn, preset, reset
  or or_1 (or_1_out, and_3_out, and_4_out);
  J_K_Flip_Flop JK3 (
    .J(and_5_out), .K(and_5_out), .clk(clock_1_out), .Q(JK1_q[2]), .reset(d_ff_8_q));  // open: Qn, preset
  J_K_Flip_Flop JK7 (
    .J(and_6_out), .K(and_6_out), .clk(clock_1_out), .Q(JK5_q[2]), .reset(d_ff_8_q));  // open: Qn, preset
  and and_7 (and_7_out, d_ff_1_q, not_5_out);
  not not_5 (not_5_out, comparator_2_eq);
  and and_8 (and_8_out, comparator_2_eq, not_2_out);
  and and_9 (and_9_out, D3_q, clock_1_out);
  and and_10 (and_10_out, JK1_q[1], JK1_q[2], JK1_q[0]);
  and and_11 (and_11_out, JK5_q[1], JK5_q[2], JK5_q[0]);
  D_Flip_Flop d_ff_2 (.D(or_2_out), .clk(clock_1_out), .Q(d_ff_2_q));  // open: Qn, preset, reset
  or or_2 (or_2_out, and_7_out, and_8_out);
  J_K_Flip_Flop j_k_ff_1 (
    .J(1'b1), .K(1'b1), .clk(and_9_out), .Q(j_k_ff_1_q[0]), .reset(d_ff_8_q));  // open: Qn, preset
  J_K_Flip_Flop JK4 (
    .J(and_10_out), .K(and_10_out), .clk(clock_1_out), .Q(JK1_q[3]), .reset(d_ff_8_q));  // open: Qn, preset
  J_K_Flip_Flop JK8 (
    .J(and_11_out), .K(and_11_out), .clk(clock_1_out), .Q(JK5_q[3]), .reset(d_ff_8_q));  // open: Qn, preset
  not not_6 (not_6_out, comparator_2_eq);
  J_K_Flip_Flop j_k_ff_2 (
    .J(j_k_ff_1_q[0]), .K(j_k_ff_1_q[0]), .clk(and_9_out), .Q(j_k_ff_1_q[1]));  // open: Qn, preset, reset
  Comparator #(.width(4)) comparator_1 (.a(JK1_q), .b(4'b1110), .eq(comparator_1_eq));  // open: gt, lt
  D_Flip_Flop D1 (.clk(clock_1_out), .Q(D1_q), .preset(comparator_1_eq), .reset(d_ff_8_q));  // open: D, Qn
  Comparator #(.width(4)) comparator_2 (.a(JK5_q), .b(4'b0111), .eq(comparator_2_eq));  // open: gt, lt
  D_Flip_Flop D3 (.clk(clock_1_out), .Q(D3_q), .preset(comparator_2_eq), .reset(d_ff_8_q));  // open: D, Qn
  and and_12 (and_12_out, d_ff_2_q, not_6_out);
  or or_3 (or_3_out, and_12_out, and_13_out);
  and and_13 (and_13_out, comparator_2_eq, xor_2_out);
  and and_14 (and_14_out, j_k_ff_1_q[1], j_k_ff_1_q[0]);
  D_Flip_Flop d_ff_3 (.D(or_3_out), .clk(clock_1_out), .Q(d_ff_3_q));  // open: Qn, preset, reset
  J_K_Flip_Flop j_k_ff_3 (
    .J(and_14_out), .K(and_14_out), .clk(and_9_out), .Q(j_k_ff_1_q[2]), .reset(d_ff_8_q));  // open: Qn, preset
  and and_15 (and_15_out, d_ff_3_q, not_7_out);
  not not_7 (not_7_out, comparator_2_eq);
  and and_16 (and_16_out, comparator_2_eq, 1'b1);
  and and_17 (and_17_out, j_k_ff_1_q[1], j_k_ff_1_q[2], j_k_ff_1_q[0]);
  D_Flip_Flop d_ff_4 (.D(or_4_out), .clk(clock_1_out), .Q(d_ff_4_q));  // open: Qn, preset, reset
  or or_4 (or_4_out, and_15_out, and_16_out);
  J_K_Flip_Flop j_k_ff_4 (
    .J(and_17_out), .K(and_17_out), .clk(and_9_out), .Q(j_k_ff_1_q[3]), .reset(d_ff_8_q));  // open: Qn, preset
  and and_18 (and_18_out, d_ff_4_q, not_8_out);
  not not_8 (not_8_out, comparator_2_eq);
  and and_19 (and_19_out, comparator_2_eq, 1'b0);
  Comparator #(.width(4)) comparator_3 (.a(j_k_ff_1_q), .b(4'b1011), .eq(comparator_3_eq));  // open: gt, lt
  D_Flip_Flop d_ff_5 (.clk(clock_1_out), .Q(d_ff_5_q), .preset(comparator_3_eq), .reset(d_ff_8_q));  // open: D, Qn
  D_Flip_Flop d_ff_6 (.D(or_5_out), .clk(clock_1_out), .Q(d_ff_6_q));  // open: Qn, preset, reset
  or or_5 (or_5_out, and_18_out, and_19_out);
  or or_6 (or_6_out[0], OR1_out, d_ff_5_q);
  or or_7 (or_6_out[1], D3_q, d_ff_5_q);
  not not_9 (not_9_out, comparator_2_eq);
  D_Flip_Flop d_ff_7 (.D(d_ff_5_q), .clk(clock_1_out), .Q(d_ff_7_q));  // open: Qn, preset, reset
  or or_8 (or_8_out, comparator_2_eq, d_ff_13_q);
  and and_20 (and_20_out, d_ff_6_q, not_9_out);
  or or_9 (or_9_out, and_20_out, and_21_out);
  and and_21 (and_21_out, comparator_2_eq, 1'b0);
  D_Flip_Flop d_ff_8 (.D(d_ff_7_q), .clk(clock_1_out), .Q(d_ff_8_q));  // open: Qn, preset, reset
  D_Flip_Flop d_ff_9 (.D(or_9_out), .clk(clock_1_out), .Q(d_ff_9_q));  // open: Qn, preset, reset
  not not_10 (not_10_out, d_ff_8_q);
  and and_22 (and_22_out, d_ff_9_q, not_11_out);
  not not_11 (not_11_out, comparator_2_eq);
  and and_23 (and_23_out, comparator_2_eq, 1'b0);
  D_Flip_Flop d_ff_10 (.D(or_10_out), .clk(clock_1_out), .Q(d_ff_10_q));  // open: Qn, preset, reset
  or or_10 (or_10_out, and_22_out, and_23_out);
  not not_12 (not_12_out, comparator_2_eq);
  D_Flip_Flop d_ff_11 (.D(or_11_out), .clk(clock_1_out), .Q(d_ff_11_q));  // open: Qn, preset, reset
  and and_24 (and_24_out, d_ff_10_q, not_12_out);
  or or_11 (or_11_out, and_24_out, and_25_out);
  and and_25 (and_25_out, comparator_2_eq, 1'b0);
  assign Master = not_10_out ? multiplexer_1_out : 1'bz;  // Controlled_Buffer controlled_buffer_1
  Multiplexer #(.select(2)) multiplexer_1 (
    .in0(OR1_out), .in1(not_4_out), .in2(1'b0), .in3(or_8_out), .out(multiplexer_1_out), .sel(or_6_out));
  and and_26 (and_26_out, d_ff_11_q, not_13_out);
  not not_13 (not_13_out, comparator_2_eq);
  and and_27 (and_27_out, comparator_2_eq, 1'b0);
  D_Flip_Flop d_ff_12 (.D(or_12_out), .clk(clock_1_out), .Q(d_ff_12_q));  // open: Qn, preset, reset
  or or_12 (or_12_out, and_26_out, and_27_out);
  and and_28 (and_28_out, d_ff_12_q, not_14_out);
  not not_14 (not_14_out, comparator_2_eq);
  and and_29 (and_29_out, comparator_2_eq, 1'b0);
  D_Flip_Flop d_ff_13 (.D(or_13_out), .clk(clock_1_out), .Q(d_ff_13_q));  // open: Qn, preset, reset
  or or_13 (or_13_out, and_28_out, and_29_out);
  Clock #(.phaseOffset(1)) clock_2 (.out(clock_2_out));
  D_Flip_Flop d_ff_14 (.D(Master), .clk(clock_2_out), .Q(out_2));  // open: Qn, preset, reset
  J_K_Flip_Flop j_k_ff_5 (
    .J(1'b1), .K(1'b1), .clk(clock_2_out), .Q(j_k_ff_5_q[0]), .reset(comparator_11_eq));  // open: Qn, preset
  D_Flip_Flop d_ff_15 (.D(out_2), .clk(clock_2_out), .Q(out_3));  // open: Qn, preset, reset
  D_Flip_Flop d_ff_16 (.D(Master), .clk(clock_2_out), .Q(out_17), .reset(comparator_11_eq));  // open: Qn, preset
  D_Flip_Flop d_ff_17 (.D(Master), .clk(clock_2_out), .Q(out_30));  // open: Qn, preset, reset
  J_K_Flip_Flop j_k_ff_6 (
    .J(j_k_ff_5_q[0]), .K(j_k_ff_5_q[0]), .clk(clock_2_out), .Q(j_k_ff_5_q[1]), .reset(comparator_11_eq));  // open: Qn, preset
  D_Flip_Flop d_ff_18 (.D(out_3), .clk(clock_2_out), .Q(out_4));  // open: Qn, preset, reset
  J_K_Flip_Flop j_k_ff_7 (
    .J(BREAK_Slave), .K(BREAK_Slave), .clk(clock_2_out), .Q(j_k_ff_7_q[0]), .reset(comparator_11_eq));  // open: Qn, preset
  D_Flip_Flop d_ff_19 (.D(out_17), .clk(clock_2_out), .Q(out_18), .reset(comparator_11_eq));  // open: Qn, preset
  J_K_Flip_Flop j_k_ff_8 (
    .J(SYNC_Slave), .K(SYNC_Slave), .clk(clock_2_out), .Q(j_k_ff_8_q[0]), .reset(comparator_11_eq));  // open: Qn, preset
  D_Flip_Flop d_ff_20 (.D(out_30), .clk(clock_2_out), .Q(out_31));  // open: Qn, preset, reset
  D_Flip_Flop d_ff_21 (.D(out_4), .clk(clock_2_out), .Q(out_5));  // open: Qn, preset, reset
  J_K_Flip_Flop j_k_ff_9 (
    .J(j_k_ff_7_q[0]), .K(j_k_ff_7_q[0]), .clk(clock_2_out), .Q(j_k_ff_7_q[1]), .reset(comparator_11_eq));  // open: Qn, preset
  D_Flip_Flop d_ff_22 (.D(out_18), .clk(clock_2_out), .Q(out_19), .reset(comparator_11_eq));  // open: Qn, preset
  J_K_Flip_Flop j_k_ff_10 (
    .J(j_k_ff_8_q[0]), .K(j_k_ff_8_q[0]), .clk(clock_2_out), .Q(j_k_ff_8_q[1]), .reset(comparator_11_eq));  // open: Qn, preset
  D_Flip_Flop d_ff_23 (.D(out_31), .clk(clock_2_out), .Q(out_32));  // open: Qn, preset, reset
  J_K_Flip_Flop j_k_ff_11 (
    .J(and_30_out), .K(and_30_out), .clk(clock_2_out), .Q(j_k_ff_5_q[2]), .reset(comparator_11_eq));  // open: Qn, preset
  and and_30 (and_30_out, j_k_ff_5_q[1], j_k_ff_5_q[0]);
  D_Flip_Flop d_ff_24 (.D(out_5), .clk(clock_2_out), .Q(out_6));  // open: Qn, preset, reset
  J_K_Flip_Flop j_k_ff_12 (
    .J(and_31_out), .K(and_31_out), .clk(clock_2_out), .Q(j_k_ff_7_q[2]), .reset(comparator_11_eq));  // open: Qn, preset
  and and_31 (and_31_out, j_k_ff_7_q[1], j_k_ff_7_q[0]);
  D_Flip_Flop d_ff_25 (.D(out_19), .clk(clock_2_out), .Q(out_20), .reset(comparator_11_eq));  // open: Qn, preset
  J_K_Flip_Flop j_k_ff_13 (
    .J(and_32_out), .K(and_32_out), .clk(clock_2_out), .Q(j_k_ff_8_q[2]), .reset(comparator_11_eq));  // open: Qn, preset
  and and_32 (and_32_out, j_k_ff_8_q[1], j_k_ff_8_q[0]);
  D_Flip_Flop d_ff_26 (.D(out_32), .clk(clock_2_out), .Q(out_33));  // open: Qn, preset, reset
  D_Flip_Flop d_ff_27 (.D(out_6), .clk(clock_2_out), .Q(out_7));  // open: Qn, preset, reset
  D_Flip_Flop d_ff_28 (.D(out_20), .clk(clock_2_out), .Q(out_21), .reset(comparator_11_eq));  // open: Qn, preset
  D_Flip_Flop d_ff_29 (.D(out_33), .clk(clock_2_out), .Q(out_34));  // open: Qn, preset, reset
  J_K_Flip_Flop j_k_ff_14 (
    .J(and_33_out), .K(and_33_out), .clk(clock_2_out), .Q(j_k_ff_5_q[3]), .reset(comparator_11_eq));  // open: Qn, preset
  and and_33 (and_33_out, j_k_ff_5_q[1], j_k_ff_5_q[2], j_k_ff_5_q[0]);
  D_Flip_Flop d_ff_30 (.D(out_7), .clk(clock_2_out), .Q(out_8));  // open: Qn, preset, reset
  J_K_Flip_Flop j_k_ff_15 (
    .J(and_34_out), .K(and_34_out), .clk(clock_2_out), .Q(j_k_ff_7_q[3]), .reset(comparator_11_eq));  // open: Qn, preset
  and and_34 (and_34_out, j_k_ff_7_q[1], j_k_ff_7_q[2], j_k_ff_7_q[0]);
  D_Flip_Flop d_ff_31 (.D(out_21), .clk(clock_2_out), .Q(out_22), .reset(comparator_11_eq));  // open: Qn, preset
  J_K_Flip_Flop j_k_ff_16 (
    .J(and_35_out), .K(and_35_out), .clk(clock_2_out), .Q(j_k_ff_8_q[3]), .reset(comparator_11_eq));  // open: Qn, preset
  and and_35 (and_35_out, j_k_ff_8_q[1], j_k_ff_8_q[2], j_k_ff_8_q[0]);
  D_Flip_Flop d_ff_32 (.D(out_34), .clk(clock_2_out), .Q(out_35));  // open: Qn, preset, reset
  D_Flip_Flop d_ff_33 (.D(out_8), .clk(clock_2_out), .Q(out_9));  // open: Qn, preset, reset
  D_Flip_Flop d_ff_34 (.D(out_22), .clk(clock_2_out), .Q(out_23), .reset(comparator_11_eq));  // open: Qn, preset
  D_Flip_Flop d_ff_35 (.D(out_35), .clk(clock_2_out), .Q(out_36));  // open: Qn, preset, reset
  Comparator #(.width(4)) comparator_4 (.a(j_k_ff_5_q), .b(4'b1110), .eq(comparator_4_eq));  // open: gt, lt
  D_Flip_Flop d_ff_36 (
    .clk(clock_2_out), .Q(d_ff_36_q), .preset(comparator_4_eq), .reset(comparator_11_eq));  // open: D, Qn
  D_Flip_Flop d_ff_37 (.D(out_9), .clk(clock_2_out), .Q(out_10));  // open: Qn, preset, reset
  Comparator #(.width(4)) comparator_5 (.a(j_k_ff_7_q), .b(4'b1001), .eq(comparator_5_eq));  // open: gt, lt
  D_Flip_Flop d_ff_38 (
    .clk(clock_2_out), .Q(d_ff_38_q), .preset(comparator_5_eq), .reset(comparator_11_eq));  // open: D, Qn
  D_Flip_Flop d_ff_39 (.D(out_23), .clk(clock_2_out), .Q(out_24), .reset(comparator_11_eq));  // open: Qn, preset
  Comparator #(.width(4)) comparator_6 (.a(j_k_ff_8_q), .b(4'b1001), .eq(comparator_6_eq));  // open: gt, lt
  D_Flip_Flop d_ff_40 (
    .clk(clock_2_out), .Q(d_ff_40_q), .preset(comparator_6_eq), .reset(comparator_11_eq));  // open: D, Qn
  D_Flip_Flop d_ff_41 (.D(out_36), .clk(clock_2_out), .Q(out_37));  // open: Qn, preset, reset
  Comparator #(.width(13)) comparator_7 (
    .a({out_14, out_13, out_12, out_11, out_10, out_9, out_8, out_7, out_6, out_5, out_4, out_3, out_2}),
    .b({13{1'b0}}), .eq(comparator_7_eq));  // open: gt, lt
  D_Flip_Flop d_ff_42 (.D(out_10), .clk(clock_2_out), .Q(out_11));  // open: Qn, preset, reset
  D_Flip_Flop d_ff_43 (.D(out_24), .clk(clock_2_out), .Q(out_25), .reset(comparator_11_eq));  // open: Qn, preset
  D_Flip_Flop d_ff_44 (.D(out_37), .clk(clock_2_out), .Q(out_38));  // open: Qn, preset, reset
  D_Flip_Flop d_ff_45 (
    .clk(comparator_7_eq), .Q(BREAK_Slave), .preset(and_36_out), .reset(comparator_11_eq));  // open: D, Qn
  and and_36 (and_36_out, d_ff_36_q, comparator_7_eq);
  D_Flip_Flop d_ff_46 (.D(out_11), .clk(clock_2_out), .Q(out_12));  // open: Qn, preset, reset
  Comparator #(.width(10)) comparator_8 (
    .a({out_26, out_25, out_24, out_23, out_22, out_21, out_20, out_19, out_18, out_17}), .b(10'hab),
    .eq(comparator_8_eq));  // open: gt, lt
  D_Flip_Flop d_ff_47 (.D(out_25), .clk(clock_2_out), .Q(out_26), .reset(comparator_11_eq));  // open: Qn, preset
  Comparator #(.width(10)) comparator_9 (
    .a({out_39, out_38, out_37, out_36, out_35, out_34, out_33, out_32, out_31, out_30}), .b(10'h9),
    .eq(comparator_9_eq));  // open: gt, lt
  D_Flip_Flop d_ff_48 (.D(out_38), .clk(clock_2_out), .Q(out_39));  // open: Qn, preset, reset
  D_Flip_Flop d_ff_49 (.D(out_12), .clk(clock_2_out), .Q(out_13));  // open: Qn, preset, reset
  D_Flip_Flop d_ff_50 (
    .clk(comparator_8_eq), .Q(SYNC_Slave), .preset(and_37_out), .reset(comparator_11_eq));  // open: D, Qn
  and and_37 (and_37_out, d_ff_38_q, comparator_8_eq);
  D_Flip_Flop d_ff_51 (
    .clk(comparator_9_eq), .Q(PID_Slave), .preset(and_38_out), .reset(comparator_11_eq));  // open: D, Qn
  and and_38 (and_38_out, d_ff_40_q, comparator_9_eq);
  D_Flip_Flop d_ff_52 (.D(out_13), .clk(clock_2_out), .Q(out_14));  // open: Qn, preset, reset
  J_K_Flip_Flop j_k_ff_17 (
    .J(PID_Slave), .K(PID_Slave), .clk(clock_2_out), .Q(j_k_ff_17_q[0]), .reset(comparator_11_eq));  // open: Qn, preset
  and and_39 (and_39_out, BREAK_Slave, SYNC_Slave, PID_Slave);
  J_K_Flip_Flop j_k_ff_18 (
    .J(j_k_ff_17_q[0]), .K(j_k_ff_17_q[0]), .clk(clock_2_out), .Q(j_k_ff_17_q[1]), .reset(comparator_11_eq));  // open: Qn, preset
  and and_40 (and_40_out, 1'b1, not_15_out);
  not not_15 (not_15_out, comparator_10_eq);
  and and_41 (and_41_out, comparator_10_eq, out_28);
  J_K_Flip_Flop j_k_ff_19 (
    .J(and_42_out), .K(and_42_out), .clk(clock_2_out), .Q(j_k_ff_17_q[2]), .reset(comparator_11_eq));  // open: Qn, preset
  and and_42 (and_42_out, j_k_ff_17_q[1], j_k_ff_17_q[0]);
  Random #(.width(2)) random_1 (.clk(and_39_out), .out({out_28, out_27}));  // open: clr, next
  D_Flip_Flop d_ff_53 (.D(or_14_out), .clk(clock_2_out), .Q(d_ff_53_q));  // open: Qn, preset, reset
  or or_14 (or_14_out, and_40_out, and_41_out);
  not not_16 (not_16_out, comparator_10_eq);
  J_K_Flip_Flop j_k_ff_20 (
    .J(and_43_out), .K(and_43_out), .clk(clock_2_out), .Q(j_k_ff_17_q[3]), .reset(comparator_11_eq));  // open: Qn, preset
  and and_43 (and_43_out, j_k_ff_17_q[1], j_k_ff_17_q[2], j_k_ff_17_q[0]);
  and and_44 (and_44_out, d_ff_53_q, not_16_out);
  or or_15 (or_15_out, and_44_out, and_45_out);
  and and_45 (and_45_out, comparator_10_eq, out_27);
  D_Flip_Flop d_ff_54 (.clk(clock_2_out), .Q(d_ff_54_q), .reset(comparator_11_eq));  // open: D, Qn, preset
  D_Flip_Flop d_ff_55 (.D(or_15_out), .clk(clock_2_out), .Q(d_ff_55_q));  // open: Qn, preset, reset
  Comparator #(.width(4)) comparator_10 (.a(j_k_ff_17_q), .b(4'b0100), .eq(comparator_10_eq));  // open: gt, lt
  and and_46 (and_46_out, d_ff_55_q, not_17_out);
  not not_17 (not_17_out, comparator_10_eq);
  and and_47 (and_47_out, comparator_10_eq, 1'b0);
  D_Flip_Flop d_ff_56 (.D(or_16_out), .clk(clock_2_out), .Q(d_ff_56_q));  // open: Qn, preset, reset
  or or_16 (or_16_out, and_46_out, and_47_out);
  and and_48 (and_48_out, d_ff_56_q, not_18_out);
  not not_18 (not_18_out, comparator_10_eq);
  and and_49 (and_49_out, comparator_10_eq, 1'b0);
  D_Flip_Flop d_ff_57 (.D(or_17_out), .clk(clock_2_out), .Q(d_ff_57_q));  // open: Qn, preset, reset
  or or_17 (or_17_out, and_48_out, and_49_out);
  not not_19 (not_19_out, comparator_10_eq);
  and and_50 (and_50_out, d_ff_57_q, not_19_out);
  or or_18 (or_18_out, and_50_out, and_51_out);
  and and_51 (and_51_out, comparator_10_eq, 1'b0);
  D_Flip_Flop d_ff_58 (.D(or_18_out), .clk(clock_2_out), .Q(d_ff_58_q));  // open: Qn, preset, reset
  and and_52 (and_52_out, d_ff_54_q, comparator_11_gt);
  assign Master = and_52_out ? Slave : 1'bz;  // Controlled_Buffer controlled_buffer_2
  and and_53 (and_53_out, d_ff_58_q, not_20_out);
  not not_20 (not_20_out, comparator_10_eq);
  and and_54 (and_54_out, comparator_10_eq, 1'b0);
  J_K_Flip_Flop j_k_ff_21 (
    .J(d_ff_54_q), .K(d_ff_54_q), .clk(clock_2_out), .Q(j_k_ff_21_q[0]));  // open: Qn, preset, reset
  D_Flip_Flop d_ff_59 (.D(or_19_out), .clk(clock_2_out), .Q(d_ff_59_q));  // open: Qn, preset, reset
  or or_19 (or_19_out, and_53_out, and_54_out);
  J_K_Flip_Flop j_k_ff_22 (
    .J(j_k_ff_21_q[0]), .K(j_k_ff_21_q[0]), .clk(clock_2_out), .Q(j_k_ff_21_q[1]));  // open: Qn, preset, reset
  not not_21 (not_21_out, comparator_10_eq);
  and and_55 (and_55_out, j_k_ff_21_q[1], j_k_ff_21_q[0]);
  D_Flip_Flop d_ff_60 (.D(or_20_out), .clk(clock_2_out), .Q(d_ff_60_q));  // open: Qn, preset, reset
  and and_56 (and_56_out, d_ff_59_q, not_21_out);
  or or_20 (or_20_out, and_56_out, and_57_out);
  and and_57 (and_57_out, comparator_10_eq, 1'b0);
  J_K_Flip_Flop j_k_ff_23 (
    .J(and_55_out), .K(and_55_out), .clk(clock_2_out), .Q(j_k_ff_21_q[2]));  // open: Qn, preset, reset
  and and_58 (and_58_out, d_ff_60_q, not_22_out);
  not not_22 (not_22_out, comparator_10_eq);
  and and_59 (and_59_out, comparator_10_eq, 1'b0);
  Comparator #(.width(3)) comparator_11 (
    .a(j_k_ff_21_q), .b(3'b111), .gt(comparator_11_gt), .eq(comparator_11_eq));  // open: lt
  D_Flip_Flop d_ff_61 (.D(or_21_out), .clk(clock_2_out), .Q(Slave));  // open: Qn, preset, reset
  or or_21 (or_21_out, and_58_out, and_59_out);

  // Notes on the sheet:
  //   Break
  //   Sync
  //   PID
  //   стоп бит
  //   старт бит
  //   при переключении мультиплексера успевает записаться новое значение
  //   тут моэно сдлетаь сброс всего
  //   Slave: Не рассчитывает PID, а только проверяет его
  //   ШИНА LIN
  //   Break
  //   Sync
  //   PID
  //   Запрос Master: BREAK + 0x55 + 0x07 Ответ Slave: 0x01 + 0xFE (данные + Checksum)
  //   Значение датчика
  //   Формирование ответа
  //   при 1 передает вход
endmodule
