// Logisim project схема_шина_LIN.circ as structural Verilog: 13 circuits, main circuit main
module main (
  output BREAK_slave,
  output master,
  output LIN,
  output SYNC_slave,
  output out_5,
  output out_6,
  output slave,
  output not_rain,
  output PID_slave,
  output light_rain,
  output normal_rain,
  output heavy_rain
);

  wire and_1_out, and_2_out, and_3_out, and_8_out, and_9_out, and_10_out, and_11_out, and_12_out, and_13_out,
       clock_1_out, clock_2_out, comparator_1_eq, comparator_2_eq, comparator_3_eq, ctr1_1_out_count,
       ctr8_1_out_count, ctr8_2_out_count, ctr9_1_out_count, ctr9_2_out_count, ctr10_1_out_count,
       ctr11_1_out_count, ctr15_1_out_count, ctr15_2_out_count, d_ff_1_q, d_ff_1_qn, d_ff_2_q, d_ff_3_q,
       d_ff_4_q, d_ff_5_q, d_ff_6_q, d_ff_7_q, d_ff_11_q, not_1_out, not_2_out, not_3_out, not_4_out,
       not_5_out, not_6_out, not_7_out, not_8_out, not_9_out, or_1_out, or_3_out, srg10_1_out_bit,
       srg12_out_par_1_out_1, srg12_out_par_1_out_10, srg_8_out_par_1_out_8, srg_8_out_par_1_out_9,
       xor_1_out, xor_2_out;
  wire [1:0] or_2_out;
  wire [9:0] srg10_out_par_1_out_9, srg10_out_par_2_out_9;
  wire [12:0] srg13_out_par_1_out_0;

  Clock clock_1 (.out(clock_1_out));
  D_Flip_Flop d_ff_1 (.D(d_ff_1_qn), .clk(clock_1_out), .Q(d_ff_1_q), .Qn(d_ff_1_qn));  // open: preset, reset
  and and_1 (and_1_out, LIN, srg12_out_par_1_out_10);
  and and_2 (and_2_out, clock_1_out, not_1_out);
  not not_1 (not_1_out, clock_1_out);
  D_Flip_Flop d_ff_2 (
    .clk(clock_1_out), .Q(d_ff_2_q), .preset(ctr15_1_out_count), .reset(srg12_out_par_1_out_1));  // open: D, Qn
  CTR15 ctr15_1 (.start(1'b1), .clock(clock_1_out), .reset(srg12_out_par_1_out_1), .out_count(ctr15_1_out_count));
  CTR8 ctr8_1 (.start(or_1_out), .clock(clock_1_out), .reset(srg12_out_par_1_out_1), .out_count(ctr8_1_out_count));
  not not_2 (not_2_out, and_3_out);
  and and_3 (and_3_out, or_1_out, d_ff_1_q);
  D_Flip_Flop d_ff_3 (
    .clk(clock_1_out), .Q(d_ff_3_q), .preset(ctr8_1_out_count), .reset(srg12_out_par_1_out_1));  // open: D, Qn
  not not_3 (not_3_out, xor_1_out);
  ExactlyOne xor_1 (.out(xor_1_out), .in0(1'b1), .in1(1'b0), .in2(1'b0), .in3(1'b0));
  ExactlyOne xor_2 (.out(xor_2_out), .in0(1'b0), .in1(1'b0), .in2(1'b0), .in3(1'b0));
  SRG_8_out_par srg_8_out_par_1 (
    .data(and_1_out), .clock(clock_1_out), .out_9(srg_8_out_par_1_out_9), .out_8(srg_8_out_par_1_out_8));  // open: reset, out_7, out_6, out_5, out_4, out_3, out_2
  CTR8 ctr8_2 (
    .start(srg12_out_par_1_out_10), .clock(clock_1_out), .reset(srg12_out_par_1_out_1),
    .out_count(ctr8_2_out_count));
  or or_1 (or_1_out, and_2_out, d_ff_2_q);
  not not_4 (not_4_out, srg_8_out_par_1_out_9);
  not not_5 (not_5_out, srg_8_out_par_1_out_8);
  and and_4 (not_rain, not_4_out, not_5_out, ctr8_2_out_count);
  not not_6 (not_6_out, srg_8_out_par_1_out_8);
  and and_5 (light_rain, srg_8_out_par_1_out_9, not_6_out, ctr8_2_out_count);
  not not_7 (not_7_out, srg_8_out_par_1_out_9);
  and and_6 (normal_rain, not_7_out, srg_8_out_par_1_out_8, ctr8_2_out_count);
  and and_7 (heavy_rain, srg_8_out_par_1_out_8, srg_8_out_par_1_out_9, ctr8_2_out_count);
  or or_2 (or_2_out[0], or_1_out, d_ff_4_q);
  or or_3 (or_3_out, ctr8_1_out_count, srg10_1_out_bit);
  or or_4 (or_2_out[1], d_ff_3_q, d_ff_4_q);
  SRG10 srg10_1 (
    .start(ctr8_1_out_count), .one_zero(1'b1), .stop_bit(1'b1), .in_5(not_3_out), .in_6(xor_2_out),
    .in_7(1'b1), .in_8(1'b0), .in_9(1'b0), .in_10(1'b0), .in_11(1'b0), .in_12(1'b0), .start_bit(1'b0),
    .clock(clock_1_out), .out_bit(srg10_1_out_bit));
  Multiplexer #(.select(2)) multiplexer_1 (
    .in0(or_1_out), .in1(not_2_out), .in2(1'b0), .in3(or_3_out), .out(master), .sel(or_2_out));
  and and_8 (and_8_out, d_ff_3_q, clock_1_out);
  assign LIN = not_8_out ? master : 1'bz;  // Controlled_Buffer controlled_buffer_1
  CTR11 ctr11_1 (.start(1'b1), .clock(and_8_out), .reset(srg12_out_par_1_out_1), .out_count(ctr11_1_out_count));
  D_Flip_Flop d_ff_4 (
    .clk(clock_1_out), .Q(d_ff_4_q), .preset(ctr11_1_out_count), .reset(srg12_out_par_1_out_1));  // open: D, Qn
  not not_8 (not_8_out, srg12_out_par_1_out_10);
  SRG12_out_par srg12_out_par_1 (
    .data(d_ff_4_q), .clock(clock_1_out), .reset(srg12_out_par_1_out_1), .out_1(srg12_out_par_1_out_1),
    .out_10(srg12_out_par_1_out_10));  // open: out_9, out_8, out_7, out_6, out_5, out_4, out_3, out_2, out_12, out_11
  Clock clock_2 (.out(clock_2_out));
  CTR15 ctr15_2 (.start(1'b1), .clock(clock_2_out), .reset(ctr10_1_out_count), .out_count(ctr15_2_out_count));
  D_Flip_Flop d_ff_5 (
    .clk(clock_2_out), .Q(d_ff_5_q), .preset(ctr15_2_out_count), .reset(ctr10_1_out_count));  // open: D, Qn
  SRG13_out_par srg13_out_par_1 (
    .data(LIN), .clock(clock_2_out), .out_9(srg13_out_par_1_out_0[9]), .out_8(srg13_out_par_1_out_0[8]),
    .out_7(srg13_out_par_1_out_0[7]), .out_6(srg13_out_par_1_out_0[6]), .out_5(srg13_out_par_1_out_0[5]),
    .out_4(srg13_out_par_1_out_0[4]), .out_3(srg13_out_par_1_out_0[3]), .out_2(srg13_out_par_1_out_0[2]),
    .out_1(srg13_out_par_1_out_0[1]), .out_0(srg13_out_par_1_out_0[0]), .out_12(srg13_out_par_1_out_0[12]),
    .out_11(srg13_out_par_1_out_0[11]), .out_10(srg13_out_par_1_out_0[10]));  // open: reset
  CTR9 ctr9_1 (.start(BREAK_slave), .clock(clock_2_out), .reset(ctr10_1_out_count), .out_count(ctr9_1_out_count));
  SRG10_out_par srg10_out_par_1 (
    .data(LIN), .clock(clock_2_out), .reset(ctr10_1_out_count), .out_9(srg10_out_par_1_out_9[0]),
    .out_8(srg10_out_par_1_out_9[1]), .out_7(srg10_out_par_1_out_9[2]), .out_6(srg10_out_par_1_out_9[3]),
    .out_5(srg10_out_par_1_out_9[4]), .out_4(srg10_out_par_1_out_9[5]), .out_3(srg10_out_par_1_out_9[6]),
    .out_2(srg10_out_par_1_out_9[7]), .out_1(srg10_out_par_1_out_9[8]), .out_0(srg10_out_par_1_out_9[9]));
  CTR9 ctr9_2 (.start(SYNC_slave), .clock(clock_2_out), .reset(ctr10_1_out_count), .out_count(ctr9_2_out_count));
  SRG10_out_par srg10_out_par_2 (
    .data(LIN), .clock(clock_2_out), .out_9(srg10_out_par_2_out_9[0]), .out_8(srg10_out_par_2_out_9[1]),
    .out_7(srg10_out_par_2_out_9[2]), .out_6(srg10_out_par_2_out_9[3]), .out_5(srg10_out_par_2_out_9[4]),
    .out_4(srg10_out_par_2_out_9[5]), .out_3(srg10_out_par_2_out_9[6]), .out_2(srg10_out_par_2_out_9[7]),
    .out_1(srg10_out_par_2_out_9[8]), .out_0(srg10_out_par_2_out_9[9]));  // open: reset
  Comparator #(.width(13)) comparator_1 (
    .a(srg13_out_par_1_out_0), .b({13{1'b0}}), .eq(comparator_1_eq));  // open: gt, lt
  D_Flip_Flop d_ff_6 (
    .clk(clock_2_out), .Q(d_ff_6_q), .preset(ctr9_1_out_count), .reset(ctr10_1_out_count));  // open: D, Qn
  Comparator #(.width(10)) comparator_2 (.a(srg10_out_par_1_out_9), .b(10'hab), .eq(comparator_2_eq));  // open: gt, lt
  D_Flip_Flop d_ff_7 (
    .clk(clock_2_out), .Q(d_ff_7_q), .preset(ctr9_2_out_count), .reset(ctr10_1_out_count));  // open: D, Qn
  Comparator #(.width(10)) comparator_3 (.a(srg10_out_par_2_out_9), .b(10'h9), .eq(comparator_3_eq));  // open: gt, lt
  and and_9 (and_9_out, d_ff_5_q, comparator_1_eq);
  D_Flip_Flop d_ff_8 (
    .clk(comparator_1_eq), .Q(BREAK_slave), .preset(and_9_out), .reset(ctr10_1_out_count));  // open: D, Qn
  and and_10 (and_10_out, d_ff_6_q, comparator_2_eq);
  D_Flip_Flop d_ff_9 (
    .clk(comparator_2_eq), .Q(SYNC_slave), .preset(and_10_out), .reset(ctr10_1_out_count));  // open: D, Qn
  and and_11 (and_11_out, d_ff_7_q, comparator_3_eq);
  D_Flip_Flop d_ff_10 (
    .clk(comparator_3_eq), .Q(PID_slave), .preset(and_11_out), .reset(ctr10_1_out_count));  // open: D, Qn
  CTR1 ctr1_1 (.start(PID_slave), .clock(clock_2_out), .reset(ctr10_1_out_count), .out_count(ctr1_1_out_count));
  Random #(.width(2)) random_1 (.clk(and_12_out), .out({out_6, out_5}));  // open: clr, next
  and and_12 (and_12_out, BREAK_slave, SYNC_slave, PID_slave);
  not not_9 (not_9_out, ctr10_1_out_count);
  and and_13 (and_13_out, d_ff_11_q, not_9_out);
  assign LIN = and_13_out ? slave : 1'bz;  // Controlled_Buffer controlled_buffer_2
  D_Flip_Flop d_ff_11 (
    .clk(clock_2_out), .Q(d_ff_11_q), .preset(ctr1_1_out_count), .reset(ctr10_1_out_count));  // open: D, Qn
  CTR10 ctr10_1 (.start(d_ff_11_q), .clock(clock_2_out), .reset(ctr10_1_out_count), .out_count(ctr10_1_out_count));
  SRG8 srg8_1 (
    .start(ctr1_1_out_count), .one_zero(1'b1), .stop_bit(out_5), .in_5(out_6), .in_6(1'b0), .in_7(1'b0),
    .in_8(1'b0), .in_9(1'b0), .in_10(1'b0), .start_bit(1'b0), .clock(clock_2_out), .out_bit(slave));

  // Notes on the sheet:
  //   B
  //   R
  //   E
  //   A
  //   K
  //   S
  //   Y
  //   N
  //   C
  //   P
  //   I
  //   D
  //   стоп бит
  //   старт бит
  //   шина LIN
  //   B
  //   R
  //   E
  //   A
  //   K
  //   S
  //   Y
  //   N
  //   C
  //   P
  //   I
  //   D
endmodule

module CTR15 (
  input  start,
  input  clock,
  input  reset,
  output out_count
);

  wire and_1_out, and_2_out;
  wire [3:0] j_k_ff_1_q;

  J_K_Flip_Flop j_k_ff_1 (.J(start), .K(start), .clk(clock), .Q(j_k_ff_1_q[0]), .reset(reset));  // open: Qn, preset
  J_K_Flip_Flop j_k_ff_2 (
    .J(j_k_ff_1_q[0]), .K(j_k_ff_1_q[0]), .clk(clock), .Q(j_k_ff_1_q[1]), .reset(reset));  // open: Qn, preset
  J_K_Flip_Flop j_k_ff_3 (
    .J(and_1_out), .K(and_1_out), .clk(clock), .Q(j_k_ff_1_q[2]), .reset(reset));  // open: Qn, preset
  and and_1 (and_1_out, j_k_ff_1_q[1], j_k_ff_1_q[0]);
  J_K_Flip_Flop j_k_ff_4 (
    .J(and_2_out), .K(and_2_out), .clk(clock), .Q(j_k_ff_1_q[3]), .reset(reset));  // open: Qn, preset
  and and_2 (and_2_out, j_k_ff_1_q[1], j_k_ff_1_q[2], j_k_ff_1_q[0]);
  Comparator #(.width(4)) comparator_1 (.a(j_k_ff_1_q), .b(4'b1110), .eq(out_count));  // open: gt, lt
endmodule

module CTR8 (
  input  start,
  input  clock,
  input  reset,
  output out_count
);

  wire and_1_out, and_2_out, and_3_out;
  wire [4:0] j_k_ff_1_q;

  J_K_Flip_Flop j_k_ff_1 (.J(start), .K(start), .clk(clock), .Q(j_k_ff_1_q[0]), .reset(reset));  // open: Qn, preset
  J_K_Flip_Flop j_k_ff_2 (
    .J(j_k_ff_1_q[0]), .K(j_k_ff_1_q[0]), .clk(clock), .Q(j_k_ff_1_q[1]), .reset(reset));  // open: Qn, preset
  J_K_Flip_Flop j_k_ff_3 (
    .J(and_1_out), .K(and_1_out), .clk(clock), .Q(j_k_ff_1_q[2]), .reset(reset));  // open: Qn, preset
  and and_1 (and_1_out, j_k_ff_1_q[1], j_k_ff_1_q[0]);
  and and_2 (and_2_out, j_k_ff_1_q[1], j_k_ff_1_q[2], j_k_ff_1_q[0]);
  J_K_Flip_Flop j_k_ff_4 (
    .J(and_2_out), .K(and_2_out), .clk(clock), .Q(j_k_ff_1_q[3]), .reset(reset));  // open: Qn, preset
  and and_3 (and_3_out, j_k_ff_1_q[1], j_k_ff_1_q[0], j_k_ff_1_q[3], j_k_ff_1_q[2]);
  J_K_Flip_Flop j_k_ff_5 (
    .J(and_3_out), .K(and_3_out), .clk(clock), .Q(j_k_ff_1_q[4]), .reset(reset));  // open: Qn, preset
  Comparator #(.width(5)) comparator_1 (.a(j_k_ff_1_q), .b(5'b01000), .eq(out_count));  // open: gt, lt
endmodule

module SRG10 (
  input  start,
  input  one_zero,
  input  stop_bit,
  input  clock,
  input  in_5,
  input  in_6,
  input  in_7,
  input  in_8,
  input  in_9,
  input  in_10,
  input  in_11,
  input  in_12,
  input  start_bit,
  output out_bit
);

  wire and_1_out, and_2_out, and_3_out, and_4_out, and_5_out, and_6_out, and_7_out, and_8_out, and_9_out,
       and_10_out, and_11_out, and_12_out, and_13_out, and_14_out, and_15_out, and_16_out, and_17_out,
       and_18_out, and_19_out, and_20_out, d_ff_1_q, d_ff_2_q, d_ff_3_q, d_ff_4_q, d_ff_5_q, d_ff_6_q,
       d_ff_7_q, d_ff_8_q, d_ff_9_q, not_1_out, not_2_out, not_3_out, not_4_out, not_5_out, not_6_out,
       not_7_out, not_8_out, not_9_out, not_10_out, or_1_out, or_2_out, or_3_out, or_4_out, or_5_out,
       or_6_out, or_7_out, or_8_out, or_9_out, or_10_out;

  not not_1 (not_1_out, start);
  and and_1 (and_1_out, one_zero, not_1_out);
  or or_1 (or_1_out, and_1_out, and_2_out);
  and and_2 (and_2_out, start, stop_bit);
  D_Flip_Flop d_ff_1 (.D(or_1_out), .clk(clock), .Q(d_ff_1_q));  // open: Qn, preset, reset
  and and_3 (and_3_out, d_ff_1_q, not_2_out);
  not not_2 (not_2_out, start);
  and and_4 (and_4_out, start, in_5);
  D_Flip_Flop d_ff_2 (.D(or_2_out), .clk(clock), .Q(d_ff_2_q));  // open: Qn, preset, reset
  or or_2 (or_2_out, and_3_out, and_4_out);
  not not_3 (not_3_out, start);
  D_Flip_Flop d_ff_3 (.D(or_3_out), .clk(clock), .Q(d_ff_3_q));  // open: Qn, preset, reset
  and and_5 (and_5_out, d_ff_2_q, not_3_out);
  or or_3 (or_3_out, and_5_out, and_6_out);
  and and_6 (and_6_out, start, in_6);
  and and_7 (and_7_out, d_ff_3_q, not_4_out);
  not not_4 (not_4_out, start);
  and and_8 (and_8_out, start, in_7);
  D_Flip_Flop d_ff_4 (.D(or_4_out), .clk(clock), .Q(d_ff_4_q));  // open: Qn, preset, reset
  or or_4 (or_4_out, and_7_out, and_8_out);
  and and_9 (and_9_out, d_ff_4_q, not_5_out);
  not not_5 (not_5_out, start);
  and and_10 (and_10_out, start, in_8);
  D_Flip_Flop d_ff_5 (.D(or_5_out), .clk(clock), .Q(d_ff_5_q));  // open: Qn, preset, reset
  or or_5 (or_5_out, and_9_out, and_10_out);
  not not_6 (not_6_out, start);
  and and_11 (and_11_out, d_ff_5_q, not_6_out);
  or or_6 (or_6_out, and_11_out, and_12_out);
  and and_12 (and_12_out, start, in_9);
  D_Flip_Flop d_ff_6 (.D(or_6_out), .clk(clock), .Q(d_ff_6_q));  // open: Qn, preset, reset
  and and_13 (and_13_out, d_ff_6_q, not_7_out);
  not not_7 (not_7_out, start);
  and and_14 (and_14_out, start, in_10);
  D_Flip_Flop d_ff_7 (.D(or_7_out), .clk(clock), .Q(d_ff_7_q));  // open: Qn, preset, reset
  or or_7 (or_7_out, and_13_out, and_14_out);
  and and_15 (and_15_out, d_ff_7_q, not_8_out);
  not not_8 (not_8_out, start);
  and and_16 (and_16_out, start, in_11);
  D_Flip_Flop d_ff_8 (.D(or_8_out), .clk(clock), .Q(d_ff_8_q));  // open: Qn, preset, reset
  or or_8 (or_8_out, and_15_out, and_16_out);
  not not_9 (not_9_out, start);
  and and_17 (and_17_out, d_ff_8_q, not_9_out);
  or or_9 (or_9_out, and_17_out, and_18_out);
  and and_18 (and_18_out, start, in_12);
  D_Flip_Flop d_ff_9 (.D(or_9_out), .clk(clock), .Q(d_ff_9_q));  // open: Qn, preset, reset
  and and_19 (and_19_out, d_ff_9_q, not_10_out);
  not not_10 (not_10_out, start);
  and and_20 (and_20_out, start, start_bit);
  D_Flip_Flop d_ff_10 (.D(or_10_out), .clk(clock), .Q(out_bit));  // open: Qn, preset, reset
  or or_10 (or_10_out, and_19_out, and_20_out);
endmodule

module CTR11 (
  input  start,
  input  clock,
  input  reset,
  output out_count
);

  wire and_1_out, and_2_out;
  wire [3:0] j_k_ff_1_q;

  J_K_Flip_Flop j_k_ff_1 (.J(start), .K(start), .clk(clock), .Q(j_k_ff_1_q[0]), .reset(reset));  // open: Qn, preset
  J_K_Flip_Flop j_k_ff_2 (
    .J(j_k_ff_1_q[0]), .K(j_k_ff_1_q[0]), .clk(clock), .Q(j_k_ff_1_q[1]), .reset(reset));  // open: Qn, preset
  J_K_Flip_Flop j_k_ff_3 (
    .J(and_1_out), .K(and_1_out), .clk(clock), .Q(j_k_ff_1_q[2]), .reset(reset));  // open: Qn, preset
  and and_1 (and_1_out, j_k_ff_1_q[1], j_k_ff_1_q[0]);
  J_K_Flip_Flop j_k_ff_4 (
    .J(and_2_out), .K(and_2_out), .clk(clock), .Q(j_k_ff_1_q[3]), .reset(reset));  // open: Qn, preset
  and and_2 (and_2_out, j_k_ff_1_q[1], j_k_ff_1_q[2], j_k_ff_1_q[0]);
  Comparator #(.width(4)) comparator_1 (.a(j_k_ff_1_q), .b(4'b1011), .eq(out_count));  // open: gt, lt
endmodule

module SRG13_out_par (
  input  data,
  input  clock,
  input  reset,
  output out_12,
  output out_11,
  output out_10,
  output out_9,
  output out_8,
  output out_7,
  output out_6,
  output out_5,
  output out_4,
  output out_3,
  output out_2,
  output out_1,
  output out_0
);

  D_Flip_Flop d_ff_1 (.D(data), .clk(clock), .Q(out_12), .reset(reset));  // open: Qn, preset
  D_Flip_Flop d_ff_2 (.D(out_12), .clk(clock), .Q(out_11), .reset(reset));  // open: Qn, preset
  D_Flip_Flop d_ff_3 (.D(out_11), .clk(clock), .Q(out_10), .reset(reset));  // open: Qn, preset
  D_Flip_Flop d_ff_4 (.D(out_10), .clk(clock), .Q(out_9), .reset(reset));  // open: Qn, preset
  D_Flip_Flop d_ff_5 (.D(out_9), .clk(clock), .Q(out_8), .reset(reset));  // open: Qn, preset
  D_Flip_Flop d_ff_6 (.D(out_8), .clk(clock), .Q(out_7), .reset(reset));  // open: Qn, preset
  D_Flip_Flop d_ff_7 (.D(out_7), .clk(clock), .Q(out_6), .reset(reset));  // open: Qn, preset
  D_Flip_Flop d_ff_8 (.D(out_6), .clk(clock), .Q(out_5), .reset(reset));  // open: Qn, preset
  D_Flip_Flop d_ff_9 (.D(out_5), .clk(clock), .Q(out_4), .reset(reset));  // open: Qn, preset
  D_Flip_Flop d_ff_10 (.D(out_4), .clk(clock), .Q(out_3), .reset(reset));  // open: Qn, preset
  D_Flip_Flop d_ff_11 (.D(out_3), .clk(clock), .Q(out_2), .reset(reset));  // open: Qn, preset
  D_Flip_Flop d_ff_12 (.D(out_2), .clk(clock), .Q(out_1), .reset(reset));  // open: Qn, preset
  D_Flip_Flop d_ff_13 (.D(out_1), .clk(clock), .Q(out_0), .reset(reset));  // open: Qn, preset
endmodule

module CTR9 (
  input  start,
  input  clock,
  input  reset,
  output out_count
);

  wire and_1_out, and_2_out, and_3_out;
  wire [4:0] j_k_ff_1_q;

  J_K_Flip_Flop j_k_ff_1 (.J(start), .K(start), .clk(clock), .Q(j_k_ff_1_q[0]), .reset(reset));  // open: Qn, preset
  J_K_Flip_Flop j_k_ff_2 (
    .J(j_k_ff_1_q[0]), .K(j_k_ff_1_q[0]), .clk(clock), .Q(j_k_ff_1_q[1]), .reset(reset));  // open: Qn, preset
  J_K_Flip_Flop j_k_ff_3 (
    .J(and_1_out), .K(and_1_out), .clk(clock), .Q(j_k_ff_1_q[2]), .reset(reset));  // open: Qn, preset
  and and_1 (and_1_out, j_k_ff_1_q[1], j_k_ff_1_q[0]);
  and and_2 (and_2_out, j_k_ff_1_q[1], j_k_ff_1_q[2], j_k_ff_1_q[0]);
  J_K_Flip_Flop j_k_ff_4 (
    .J(and_2_out), .K(and_2_out), .clk(clock), .Q(j_k_ff_1_q[3]), .reset(reset));  // open: Qn, preset
  and and_3 (and_3_out, j_k_ff_1_q[1], j_k_ff_1_q[0], j_k_ff_1_q[3], j_k_ff_1_q[2]);
  J_K_Flip_Flop j_k_ff_5 (
    .J(and_3_out), .K(and_3_out), .clk(clock), .Q(j_k_ff_1_q[4]), .reset(reset));  // open: Qn, preset
  Comparator #(.width(5)) comparator_1 (.a(j_k_ff_1_q), .b(5'b01001), .eq(out_count));  // open: gt, lt
endmodule

module SRG10_out_par (
  input  data,
  input  clock,
  input  reset,
  output out_9,
  output out_8,
  output out_7,
  output out_6,
  output out_5,
  output out_4,
  output out_3,
  output out_2,
  output out_1,
  output out_0
);

  D_Flip_Flop d_ff_1 (.D(data), .clk(clock), .Q(out_9), .reset(reset));  // open: Qn, preset
  D_Flip_Flop d_ff_2 (.D(out_9), .clk(clock), .Q(out_8), .reset(reset));  // open: Qn, preset
  D_Flip_Flop d_ff_3 (.D(out_8), .clk(clock), .Q(out_7), .reset(reset));  // open: Qn, preset
  D_Flip_Flop d_ff_4 (.D(out_7), .clk(clock), .Q(out_6), .reset(reset));  // open: Qn, preset
  D_Flip_Flop d_ff_5 (.D(out_6), .clk(clock), .Q(out_5), .reset(reset));  // open: Qn, preset
  D_Flip_Flop d_ff_6 (.D(out_5), .clk(clock), .Q(out_4), .reset(reset));  // open: Qn, preset
  D_Flip_Flop d_ff_7 (.D(out_4), .clk(clock), .Q(out_3), .reset(reset));  // open: Qn, preset
  D_Flip_Flop d_ff_8 (.D(out_3), .clk(clock), .Q(out_2), .reset(reset));  // open: Qn, preset
  D_Flip_Flop d_ff_9 (.D(out_2), .clk(clock), .Q(out_1), .reset(reset));  // open: Qn, preset
  D_Flip_Flop d_ff_10 (.D(out_1), .clk(clock), .Q(out_0), .reset(reset));  // open: Qn, preset
endmodule

module CTR1 (
  input  start,
  input  clock,
  input  reset,
  output out_count
);

  wire and_1_out, and_2_out;
  wire [3:0] j_k_ff_1_q;

  J_K_Flip_Flop j_k_ff_1 (.J(start), .K(start), .clk(clock), .Q(j_k_ff_1_q[0]), .reset(reset));  // open: Qn, preset
  J_K_Flip_Flop j_k_ff_2 (
    .J(j_k_ff_1_q[0]), .K(j_k_ff_1_q[0]), .clk(clock), .Q(j_k_ff_1_q[1]), .reset(reset));  // open: Qn, preset
  J_K_Flip_Flop j_k_ff_3 (
    .J(and_1_out), .K(and_1_out), .clk(clock), .Q(j_k_ff_1_q[2]), .reset(reset));  // open: Qn, preset
  and and_1 (and_1_out, j_k_ff_1_q[1], j_k_ff_1_q[0]);
  J_K_Flip_Flop j_k_ff_4 (
    .J(and_2_out), .K(and_2_out), .clk(clock), .Q(j_k_ff_1_q[3]), .reset(reset));  // open: Qn, preset
  and and_2 (and_2_out, j_k_ff_1_q[1], j_k_ff_1_q[2], j_k_ff_1_q[0]);
  Comparator #(.width(4)) comparator_1 (.a(j_k_ff_1_q), .b(4'b0001), .eq(out_count));  // open: gt, lt
endmodule

module SRG8 (
  input  start,
  input  one_zero,
  input  stop_bit,
  input  clock,
  input  in_5,
  input  in_6,
  input  in_7,
  input  in_8,
  input  in_9,
  input  in_10,
  input  start_bit,
  output out_bit
);

  wire and_1_out, and_2_out, and_3_out, and_4_out, and_5_out, and_6_out, and_7_out, and_8_out, and_9_out,
       and_10_out, and_11_out, and_12_out, and_13_out, and_14_out, and_15_out, and_16_out, d_ff_1_q,
       d_ff_2_q, d_ff_3_q, d_ff_4_q, d_ff_5_q, d_ff_6_q, d_ff_7_q, not_1_out, not_2_out, not_3_out,
       not_4_out, not_5_out, not_6_out, not_7_out, not_8_out, or_1_out, or_2_out, or_3_out, or_4_out,
       or_5_out, or_6_out, or_7_out, or_8_out;

  not not_1 (not_1_out, start);
  and and_1 (and_1_out, one_zero, not_1_out);
  or or_1 (or_1_out, and_1_out, and_2_out);
  and and_2 (and_2_out, start, stop_bit);
  D_Flip_Flop d_ff_1 (.D(or_1_out), .clk(clock), .Q(d_ff_1_q));  // open: Qn, preset, reset
  and and_3 (and_3_out, d_ff_1_q, not_2_out);
  not not_2 (not_2_out, start);
  and and_4 (and_4_out, start, in_5);
  D_Flip_Flop d_ff_2 (.D(or_2_out), .clk(clock), .Q(d_ff_2_q));  // open: Qn, preset, reset
  or or_2 (or_2_out, and_3_out, and_4_out);
  not not_3 (not_3_out, start);
  D_Flip_Flop d_ff_3 (.D(or_3_out), .clk(clock), .Q(d_ff_3_q));  // open: Qn, preset, reset
  and and_5 (and_5_out, d_ff_2_q, not_3_out);
  or or_3 (or_3_out, and_5_out, and_6_out);
  and and_6 (and_6_out, start, in_6);
  and and_7 (and_7_out, d_ff_3_q, not_4_out);
  not not_4 (not_4_out, start);
  and and_8 (and_8_out, start, in_7);
  D_Flip_Flop d_ff_4 (.D(or_4_out), .clk(clock), .Q(d_ff_4_q));  // open: Qn, preset, reset
  or or_4 (or_4_out, and_7_out, and_8_out);
  and and_9 (and_9_out, d_ff_4_q, not_5_out);
  not not_5 (not_5_out, start);
  and and_10 (and_10_out, start, in_8);
  D_Flip_Flop d_ff_5 (.D(or_5_out), .clk(clock), .Q(d_ff_5_q));  // open: Qn, preset, reset
  or or_5 (or_5_out, and_9_out, and_10_out);
  not not_6 (not_6_out, start);
  and and_11 (and_11_out, d_ff_5_q, not_6_out);
  or or_6 (or_6_out, and_11_out, and_12_out);
  and and_12 (and_12_out, start, in_9);
  D_Flip_Flop d_ff_6 (.D(or_6_out), .clk(clock), .Q(d_ff_6_q));  // open: Qn, preset, reset
  and and_13 (and_13_out, d_ff_6_q, not_7_out);
  not not_7 (not_7_out, start);
  and and_14 (and_14_out, start, in_10);
  D_Flip_Flop d_ff_7 (.D(or_7_out), .clk(clock), .Q(d_ff_7_q));  // open: Qn, preset, reset
  or or_7 (or_7_out, and_13_out, and_14_out);
  and and_15 (and_15_out, d_ff_7_q, not_8_out);
  not not_8 (not_8_out, start);
  and and_16 (and_16_out, start, start_bit);
  D_Flip_Flop d_ff_8 (.D(or_8_out), .clk(clock), .Q(out_bit));  // open: Qn, preset, reset
  or or_8 (or_8_out, and_15_out, and_16_out);
endmodule

module CTR10 (
  input  start,
  input  clock,
  input  reset,
  output out_count
);

  wire and_1_out, and_2_out;
  wire [3:0] j_k_ff_1_q;

  J_K_Flip_Flop j_k_ff_1 (.J(start), .K(start), .clk(clock), .Q(j_k_ff_1_q[0]), .reset(reset));  // open: Qn, preset
  J_K_Flip_Flop j_k_ff_2 (
    .J(j_k_ff_1_q[0]), .K(j_k_ff_1_q[0]), .clk(clock), .Q(j_k_ff_1_q[1]), .reset(reset));  // open: Qn, preset
  J_K_Flip_Flop j_k_ff_3 (
    .J(and_1_out), .K(and_1_out), .clk(clock), .Q(j_k_ff_1_q[2]), .reset(reset));  // open: Qn, preset
  and and_1 (and_1_out, j_k_ff_1_q[1], j_k_ff_1_q[0]);
  J_K_Flip_Flop j_k_ff_4 (
    .J(and_2_out), .K(and_2_out), .clk(clock), .Q(j_k_ff_1_q[3]), .reset(reset));  // open: Qn, preset
  and and_2 (and_2_out, j_k_ff_1_q[1], j_k_ff_1_q[2], j_k_ff_1_q[0]);
  Comparator #(.width(4)) comparator_1 (.a(j_k_ff_1_q), .b(4'b1010), .eq(out_count));  // open: gt, lt
endmodule

module SRG_8_out_par (
  input  data,
  input  clock,
  input  reset,
  output out_9,
  output out_8,
  output out_7,
  output out_6,
  output out_5,
  output out_4,
  output out_3,
  output out_2
);

  D_Flip_Flop d_ff_1 (.D(data), .clk(clock), .Q(out_9), .reset(reset));  // open: Qn, preset
  D_Flip_Flop d_ff_2 (.D(out_9), .clk(clock), .Q(out_8), .reset(reset));  // open: Qn, preset
  D_Flip_Flop d_ff_3 (.D(out_8), .clk(clock), .Q(out_7), .reset(reset));  // open: Qn, preset
  D_Flip_Flop d_ff_4 (.D(out_7), .clk(clock), .Q(out_6), .reset(reset));  // open: Qn, preset
  D_Flip_Flop d_ff_5 (.D(out_6), .clk(clock), .Q(out_5), .reset(reset));  // open: Qn, preset
  D_Flip_Flop d_ff_6 (.D(out_5), .clk(clock), .Q(out_4), .reset(reset));  // open: Qn, preset
  D_Flip_Flop d_ff_7 (.D(out_4), .clk(clock), .Q(out_3), .reset(reset));  // open: Qn, preset
  D_Flip_Flop d_ff_8 (.D(out_3), .clk(clock), .Q(out_2), .reset(reset));  // open: Qn, preset
endmodule

module SRG12_out_par (
  input  data,
  input  clock,
  input  reset,
  output out_12,
  output out_11,
  output out_10,
  output out_9,
  output out_8,
  output out_7,
  output out_6,
  output out_5,
  output out_4,
  output out_3,
  output out_2,
  output out_1
);

  D_Flip_Flop d_ff_1 (.D(data), .clk(clock), .Q(out_12), .reset(reset));  // open: Qn, preset
  D_Flip_Flop d_ff_2 (.D(out_12), .clk(clock), .Q(out_11), .reset(reset));  // open: Qn, preset
  D_Flip_Flop d_ff_3 (.D(out_11), .clk(clock), .Q(out_10), .reset(reset));  // open: Qn, preset
  D_Flip_Flop d_ff_4 (.D(out_10), .clk(clock), .Q(out_9), .reset(reset));  // open: Qn, preset
  D_Flip_Flop d_ff_5 (.D(out_9), .clk(clock), .Q(out_8), .reset(reset));  // open: Qn, preset
  D_Flip_Flop d_ff_6 (.D(out_8), .clk(clock), .Q(out_7), .reset(reset));  // open: Qn, preset
  D_Flip_Flop d_ff_7 (.D(out_7), .clk(clock), .Q(out_6), .reset(reset));  // open: Qn, preset
  D_Flip_Flop d_ff_8 (.D(out_6), .clk(clock), .Q(out_5), .reset(reset));  // open: Qn, preset
  D_Flip_Flop d_ff_9 (.D(out_5), .clk(clock), .Q(out_4), .reset(reset));  // open: Qn, preset
  D_Flip_Flop d_ff_10 (.D(out_4), .clk(clock), .Q(out_3), .reset(reset));  // open: Qn, preset
  D_Flip_Flop d_ff_11 (.D(out_3), .clk(clock), .Q(out_2), .reset(reset));  // open: Qn, preset
  D_Flip_Flop d_ff_12 (.D(out_2), .clk(clock), .Q(out_1), .reset(reset));  // open: Qn, preset
endmodule
